# Fritzing sketch schematics (saved by Fritzing 0.9.4)
breadboards: 1

parts:
  Componente1 = Julieta
  Componente2 = Encoder E2-Q2
  Componente3 = Encoder E2-Q2
  M1 = DC Motor
  M2 = DC Motor  # not connected
  C1 = Ceramic Capacitor [capacitance=100nF package="100 mil [THT, multilayer]"]  # not connected
  R1 = Slide Potentiometer [maximum_resistance=100kΩ]
  R2 = Resistor [tolerance=±5% resistance=51k package=THT]
  R3 = Resistor [tolerance=±5% resistance=75k package=THT]
  D1 = Zener Diode [part_number=1n4733 breakdown_voltage=5.1V package="300 mil [THT]"]
  C2 = Ceramic Capacitor [capacitance=10pF package="100 mil [THT, multilayer]"]
  R4 = Resistor [tolerance=±5% resistance=220 package=THT]
  C3 = Ceramic Capacitor [capacitance=100nF package="100 mil [THT, multilayer]"]
  D2 = Rectifier Diode [part_number=1N4001 package="300 mil [THT]"]  # not connected
  R5 = Resistor [tolerance=±5% resistance=220 package=THT]
  R6 = Resistor [tolerance=±5% resistance=220 package=THT]  # not connected
  D3 = Rectifier Diode [part_number=1N4001 package="300 mil [THT]"]  # not connected
  R7 = Resistor [tolerance=±5% resistance=220 package=THT]
  R8 = Resistor [tolerance=±5% resistance=220 package=THT]  # not connected
  D4 = Rectifier Diode [part_number=1N4001 package="300 mil [THT]"]  # not connected
  C4 = Ceramic Capacitor [capacitance=100nF package="100 mil [THT, multilayer]"]
  D5 = Rectifier Diode [part_number=1N4001 package="300 mil [THT]"]  # not connected
  C5 = Ceramic Capacitor [capacitance=100nF package="100 mil [THT, multilayer]"]
  Grove1 = Grove OLED 128x96

nets:
  N1: Componente1.pin_2, Componente1.pin_33, R1.wiper
  N2: Componente1.pin_3, Componente1.pin_34, R2.Pin_1, R3.Pin_0, D1.cathode, C2.0
  N3: Componente1.pin_4, R4.Pin_1, C3.1
  N4: Componente1.pin_5, Componente1.pin_36, Grove1.SDA
  N5: Componente1.pin_6, Componente1.pin_37, Grove1.SCL
  N6: Componente1.pin_7, R2.Pin_0
  GND: Componente1.pin_9, Componente1.pin_28, Componente1.pin_68, Componente1.pin_75, Componente1.pin_90, Componente1.pin_96, Componente1.pin_97, Componente2.GND, Componente3.GND, R1.leg1, R3.Pin_1, D1.anode, C2.1, C3.0, C4.0, C5.1, Grove1.GND
  N7: Componente1.pin_16, Componente1.pin_42, Componente3.Canal_2
  N8: Componente1.pin_17, Componente1.pin_43, Componente2.Canal_2
  N9: Componente1.pin_18, Componente1.pin_44, Componente3.Canal_1
  N10: Componente1.pin_19, Componente1.pin_45, Componente2.Canal_1
  N11: Componente1.pin_20, R4.Pin_0
  N12: Componente1.pin_38, R5.Pin_0
  N13: Componente1.pin_39, R7.Pin_0
  VCC: Componente1.pin_55, Componente1.pin_60, Componente1.pin_82, Componente1.pin_89, Componente2.VCC, Componente3.VCC, R1.leg2, Grove1.VCC
  N14: Componente1.pin_126, M1.pin_1
  N15: Componente1.pin_127, M1.pin_2

custom parts:
  Encoder E2-Q2: Encoder Óptico de Quadratura para o motor com caixa de redução e eixo duplo de 3 - 6 V.
